# Fritzing sketch lightsaber (saved by Fritzing 1.0.6)
breadboards: 1

parts:
  U1 = Arduino Nano (Rev3.0)
  U2 = ADXL345 [package=lga14]
  U3 = MCP4725 [package=SOT23-6]
  SP1 = SPEAKER [package=pcb_mount_speaker]

nets:
  GND: U1.GND, U2.GND, U2.VSS, U2.SDO, U3.VSS, U3.AO, SP1.-
  N1: U1.D2, U2.INT1
  N2: U1.A5, U2.SCL, U3.SCL
  N3: U1.A4, U2.SDA, U3.SDA
  VDD: U1.3V3, U2.VDD, U2.CS, U3.VDD
  N4: U3.VOUT, SP1.+
